# Fritzing sketch elec (saved by Fritzing 0.9.9b)
circuit board: 3.6cm x 2.8cm
breadboards: 1

parts:
  MCU1 = Raspberry Pi Zero
  LED1 = LEDs [package=led10mm]
  R1 = Resistor [tolerance=±5% power=0.25 resistance=220 package=THT]
  IR1 = TSOP312.., 314.. [package=THT]
  Q1 = NPN-Transistor [package="SOT-23 [SMD]"]

nets:
  N1: MCU1.pin_2, LED1.A, IR1.Vs
  N2: MCU1.pin_6, MCU1.pin_39, IR1.GND, Q1.2
  N3: MCU1.pin_35, IR1.Data
  N4: MCU1.pin_37, R1.Pin_1
  N5: LED1.C, Q1.1
  N6: R1.Pin_0, Q1.0
